// Logisim project codebook.circ as structural Verilog
module main (
);
endmodule

module half_adder (
  input  A_in,
  input  B_in,
  output Sum_out,
  output Carry_out
);

  xor xor_1 (Sum_out, A_in, B_in);
  and and_1 (Carry_out, A_in, B_in);
endmodule

module full_adder (
  input  Carry_in,
  input  A_in,
  input  B_in,
  output Sum_out,
  output Carry_out
);

  wire half_adder_1_carry_out, half_adder_2_carry_out, half_adder_2_sum_out;

  half_adder half_adder_1 (
    .A_in(Carry_in), .B_in(half_adder_2_sum_out), .Sum_out(Sum_out), .Carry_out(half_adder_1_carry_out));
  half_adder half_adder_2 (
    .A_in(A_in), .B_in(B_in), .Sum_out(half_adder_2_sum_out), .Carry_out(half_adder_2_carry_out));
  or or_1 (Carry_out, half_adder_1_carry_out, half_adder_2_carry_out);
endmodule

module _8_bit_adder (
  input  Carry_in,
  input  A0,
  input  B0,
  input  A1,
  input  B1,
  input  A2,
  input  B2,
  input  A3,
  input  B3,
  input  A4,
  input  B4,
  input  A5,
  input  B5,
  input  A6,
  input  B6,
  input  A7,
  input  B7,
  output S0,
  output S1,
  output S2,
  output S3,
  output S4,
  output S5,
  output S6,
  output S7,
  output Carry_out
);

  wire full_adder_1_carry_out, full_adder_2_carry_out, full_adder_3_carry_out, full_adder_4_carry_out,
       full_adder_5_carry_out, full_adder_6_carry_out, full_adder_7_carry_out;

  full_adder full_adder_1 (.Carry_in(Carry_in), .A_in(A0), .B_in(B0), .Sum_out(S0), .Carry_out(full_adder_1_carry_out));
  full_adder full_adder_2 (
    .Carry_in(full_adder_1_carry_out), .A_in(A1), .B_in(B1), .Sum_out(S1), .Carry_out(full_adder_2_carry_out));
  full_adder full_adder_3 (
    .Carry_in(full_adder_2_carry_out), .A_in(A2), .B_in(B2), .Sum_out(S2), .Carry_out(full_adder_3_carry_out));
  full_adder full_adder_4 (
    .Carry_in(full_adder_3_carry_out), .A_in(A3), .B_in(B3), .Sum_out(S3), .Carry_out(full_adder_4_carry_out));
  full_adder full_adder_5 (
    .Carry_in(full_adder_4_carry_out), .A_in(A4), .B_in(B4), .Sum_out(S4), .Carry_out(full_adder_5_carry_out));
  full_adder full_adder_6 (
    .Carry_in(full_adder_5_carry_out), .A_in(A5), .B_in(B5), .Sum_out(S5), .Carry_out(full_adder_6_carry_out));
  full_adder full_adder_7 (
    .Carry_in(full_adder_6_carry_out), .A_in(A6), .B_in(B6), .Sum_out(S6), .Carry_out(full_adder_7_carry_out));
  full_adder full_adder_8 (
    .Carry_in(full_adder_7_carry_out), .A_in(A7), .B_in(B7), .Sum_out(S7), .Carry_out(Carry_out));
endmodule

module ones_complement (
  input  [7:0] In,
  input  Negate,
  output [7:0] Out
);

  xor xor_1 (Out[0], In[0], Negate);
  xor xor_2 (Out[1], In[1], Negate);
  xor xor_3 (Out[2], In[2], Negate);
  xor xor_4 (Out[3], In[3], Negate);
  xor xor_5 (Out[4], In[4], Negate);
  xor xor_6 (Out[5], In[5], Negate);
  xor xor_7 (Out[6], In[6], Negate);
  xor xor_8 (Out[7], In[7], Negate);
endmodule

module subadder (
  input  [7:0] B_in,
  input  Sub,
  input  [7:0] A_in,
  output [7:0] Out,
  output Overflow_underflow
);

  wire n8_bit_adder_splitter_1_carry_out;
  wire [7:0] ones_complement_1_out;

  xor xor_1 (Overflow_underflow, Sub, n8_bit_adder_splitter_1_carry_out);
  ones_complement ones_complement_1 (.In(B_in), .Negate(Sub), .Out(ones_complement_1_out));
  _8_bit_adder__splitter u_8_bit_adder_splitter_1 (
    .A_in(A_in), .B_in(ones_complement_1_out), .Out(Out), .Carry_in(Sub),
    .Carry_out(n8_bit_adder_splitter_1_carry_out));
endmodule

module latch__D_flip_flop (
  input  Clock,
  input  Set,
  output Q,
  output Qbar
);

  wire and_1_out, and_2_out, not_1_out;

  not not_1 (not_1_out, Set);
  and and_1 (and_1_out, not_1_out, Clock);
  and and_2 (and_2_out, Clock, Set);
  nor nor_1 (Q, and_1_out, Qbar);
  nor nor_2 (Qbar, Q, and_2_out);
endmodule

module _8_bit_adder__splitter (
  input  [7:0] A_in,
  input  Carry_in,
  input  [7:0] B_in,
  output [7:0] Out,
  output Carry_out
);

  _8_bit_adder u_8_bit_adder_1 (
    .A0(A_in[0]), .B0(B_in[0]), .A1(A_in[1]), .B1(B_in[1]), .A2(A_in[2]), .B2(B_in[2]), .A3(A_in[3]),
    .B3(B_in[3]), .A4(A_in[4]), .B4(B_in[4]), .A5(A_in[5]), .B5(B_in[5]), .A6(A_in[6]), .B6(B_in[6]),
    .A7(A_in[7]), .B7(B_in[7]), .Carry_in(Carry_in), .Carry_out(Carry_out), .S0(Out[0]), .S1(Out[1]),
    .S2(Out[2]), .S3(Out[3]), .S4(Out[4]), .S5(Out[5]), .S6(Out[6]), .S7(Out[7]));
endmodule

module _8_bit_latch (
  input  [7:0] In,
  input  Clock,
  output [7:0] Out
);

  latch__D_flip_flop latch_d_flip_flop_1 (.Clock(Clock), .Set(In[7]), .Q(Out[7]));  // open: Qbar
  latch__D_flip_flop latch_d_flip_flop_2 (.Clock(Clock), .Set(In[5]), .Q(Out[5]));  // open: Qbar
  latch__D_flip_flop latch_d_flip_flop_3 (.Clock(Clock), .Set(In[6]), .Q(Out[6]));  // open: Qbar
  latch__D_flip_flop latch_d_flip_flop_4 (.Clock(Clock), .Set(In[4]), .Q(Out[4]));  // open: Qbar
  latch__D_flip_flop latch_d_flip_flop_5 (.Clock(Clock), .Set(In[3]), .Q(Out[3]));  // open: Qbar
  latch__D_flip_flop latch_d_flip_flop_6 (.Clock(Clock), .Set(In[1]), .Q(Out[1]));  // open: Qbar
  latch__D_flip_flop latch_d_flip_flop_7 (.Clock(Clock), .Set(In[2]), .Q(Out[2]));  // open: Qbar
  latch__D_flip_flop latch_d_flip_flop_8 (.Clock(Clock), .Set(In[0]), .Q(Out[0]));  // open: Qbar
endmodule

module _2_to_1_selector_unit (
  input  B,
  input  Select,
  input  A,
  output out_4
);

  wire and_1_out, and_2_out, not_1_out;

  not not_1 (not_1_out, Select);
  and and_1 (and_1_out, B, Select);
  and and_2 (and_2_out, A, not_1_out);
  or or_1 (out_4, and_1_out, and_2_out);
endmodule

module modified_latch (
  input  Clear,
  input  Clock,
  input  Set,
  output Q,
  output Qbar
);

  wire and_1_out, and_2_out, not_1_out, or_1_out;

  not not_1 (not_1_out, Set);
  and and_1 (and_1_out, not_1_out, Clock);
  and and_2 (and_2_out, Clock, Set);
  or or_1 (or_1_out, Clear, and_1_out);
  nor nor_1 (Q, or_1_out, Qbar);
  nor nor_2 (Qbar, Q, and_2_out);
endmodule

module edge_triggered_D_flip_flop (
  input  Data,
  input  Clock,
  output Q,
  output Qbar
);

  wire and_1_out, and_2_out, and_3_out, and_4_out, nor_1_out, nor_2_out, not_1_out, not_2_out;

  not not_1 (not_1_out, Clock);
  not not_2 (not_2_out, Data);
  and and_1 (and_1_out, Data, not_1_out);
  and and_2 (and_2_out, not_1_out, not_2_out);
  nor nor_1 (nor_1_out, and_1_out, nor_2_out);
  nor nor_2 (nor_2_out, nor_1_out, and_2_out);
  and and_3 (and_3_out, nor_1_out, Clock);
  and and_4 (and_4_out, Clock, nor_2_out);
  nor nor_3 (Q, and_3_out, Qbar);
  nor nor_4 (Qbar, Q, and_4_out);
endmodule

module broken_ripple_counter (
  input  Clock,
  output Clockbar,
  output Q0,
  output Q1,
  output Q2,
  output Q3,
  output Q4,
  output Q5,
  output Q6,
  output Q7
);

  wire edge_triggered_d_flip_flop_1_qbar, edge_triggered_d_flip_flop_2_qbar,
       edge_triggered_d_flip_flop_3_qbar, edge_triggered_d_flip_flop_4_qbar,
       edge_triggered_d_flip_flop_5_qbar, edge_triggered_d_flip_flop_6_qbar,
       edge_triggered_d_flip_flop_7_qbar, edge_triggered_d_flip_flop_8_qbar;

  not not_1 (Clockbar, Clock);
  edge_triggered_D_flip_flop edge_triggered_d_flip_flop_1 (
    .Data(edge_triggered_d_flip_flop_1_qbar), .Clock(Clock), .Q(Q0), .Qbar(edge_triggered_d_flip_flop_1_qbar));
  edge_triggered_D_flip_flop edge_triggered_d_flip_flop_2 (
    .Data(edge_triggered_d_flip_flop_2_qbar), .Clock(edge_triggered_d_flip_flop_1_qbar), .Q(Q1),
    .Qbar(edge_triggered_d_flip_flop_2_qbar));
  edge_triggered_D_flip_flop edge_triggered_d_flip_flop_3 (
    .Data(edge_triggered_d_flip_flop_3_qbar), .Clock(edge_triggered_d_flip_flop_2_qbar), .Q(Q2),
    .Qbar(edge_triggered_d_flip_flop_3_qbar));
  edge_triggered_D_flip_flop edge_triggered_d_flip_flop_4 (
    .Data(edge_triggered_d_flip_flop_4_qbar), .Clock(edge_triggered_d_flip_flop_5_qbar), .Q(Q4),
    .Qbar(edge_triggered_d_flip_flop_4_qbar));
  edge_triggered_D_flip_flop edge_triggered_d_flip_flop_5 (
    .Data(edge_triggered_d_flip_flop_5_qbar), .Clock(edge_triggered_d_flip_flop_3_qbar), .Q(Q3),
    .Qbar(edge_triggered_d_flip_flop_5_qbar));
  edge_triggered_D_flip_flop edge_triggered_d_flip_flop_6 (
    .Data(edge_triggered_d_flip_flop_6_qbar), .Clock(edge_triggered_d_flip_flop_4_qbar), .Q(Q5),
    .Qbar(edge_triggered_d_flip_flop_6_qbar));
  edge_triggered_D_flip_flop edge_triggered_d_flip_flop_7 (
    .Data(edge_triggered_d_flip_flop_7_qbar), .Clock(edge_triggered_d_flip_flop_6_qbar), .Q(Q6),
    .Qbar(edge_triggered_d_flip_flop_7_qbar));
  edge_triggered_D_flip_flop edge_triggered_d_flip_flop_8 (
    .Data(edge_triggered_d_flip_flop_8_qbar), .Clock(edge_triggered_d_flip_flop_7_qbar), .Q(Q7),
    .Qbar(edge_triggered_d_flip_flop_8_qbar));
endmodule

module actual_ripple_counter (
  output not_Clock,
  output out_2,
  output out_3,
  output out_4
);

  wire clock_1_out, d_ff_1_qn, d_ff_2_qn, d_ff_3_qn;

  not not_1 (not_Clock, clock_1_out);
  Clock clock_1 (.out(clock_1_out));
  D_Flip_Flop d_ff_1 (.clk(clock_1_out), .D(d_ff_1_qn), .Q(out_2), .Qn(d_ff_1_qn));  // open: preset, en, reset
  D_Flip_Flop d_ff_2 (.clk(d_ff_1_qn), .D(d_ff_2_qn), .Q(out_3), .Qn(d_ff_2_qn));  // open: preset, en, reset
  D_Flip_Flop d_ff_3 (.clk(d_ff_2_qn), .D(d_ff_3_qn), .Q(out_4), .Qn(d_ff_3_qn));  // open: preset, en, reset
endmodule

module _2_to_1_selector (
  input  Sel,
  input  A0,
  input  B0,
  input  A1,
  input  B1,
  input  A2,
  input  B2,
  input  A3,
  input  B3,
  input  A4,
  input  B4,
  input  A5,
  input  B5,
  input  A6,
  input  B6,
  input  A7,
  input  B7,
  output [7:0] Out
);

  _2_to_1_selector_unit u_2_to_1_selector_unit_1 (.B(A0), .Select(Sel), .A(B0), .out_4(Out[0]));
  _2_to_1_selector_unit u_2_to_1_selector_unit_2 (.B(A1), .Select(Sel), .A(B1), .out_4(Out[1]));
  _2_to_1_selector_unit u_2_to_1_selector_unit_3 (.B(A2), .Select(Sel), .A(B2), .out_4(Out[2]));
  _2_to_1_selector_unit u_2_to_1_selector_unit_4 (.B(A3), .Select(Sel), .A(B3), .out_4(Out[3]));
  _2_to_1_selector_unit u_2_to_1_selector_unit_5 (.B(A4), .Select(Sel), .A(B4), .out_4(Out[4]));
  _2_to_1_selector_unit u_2_to_1_selector_unit_6 (.B(A5), .Select(Sel), .A(B5), .out_4(Out[5]));
  _2_to_1_selector_unit u_2_to_1_selector_unit_7 (.B(A6), .Select(Sel), .A(B6), .out_4(Out[6]));
  _2_to_1_selector_unit u_2_to_1_selector_unit_8 (.B(A7), .Select(Sel), .A(B7), .out_4(Out[7]));
endmodule

module _2_to_1_selector__splitter (
  input  [7:0] A_in,
  input  Sel,
  input  [7:0] B_in,
  output [7:0] Out
);

  _2_to_1_selector u_2_to_1_selector_1 (
    .A0(A_in[0]), .B0(B_in[0]), .A1(A_in[1]), .B1(B_in[1]), .A2(A_in[2]), .B2(B_in[2]), .A3(A_in[3]),
    .B3(B_in[3]), .A4(A_in[4]), .B4(B_in[4]), .A5(A_in[5]), .B5(B_in[5]), .A6(A_in[6]), .B6(B_in[6]),
    .A7(A_in[7]), .B7(B_in[7]), .Sel(Sel), .Out(Out));
endmodule

module adding_machine (
  input  [7:0] Switches,
  input  Switches_2,
  input  Switches_3,
  input  CI,
  output CO,
  output [7:0] out_6
);

  wire [7:0] n2_to_1_selector_splitter_1_out, n8_bit_latch_1_out;

  _8_bit_latch u_8_bit_latch_1 (.In(out_6), .Clock(Switches_2), .Out(n8_bit_latch_1_out));
  _2_to_1_selector__splitter u_2_to_1_selector_splitter_1 (
    .A_in(Switches), .B_in(n8_bit_latch_1_out), .Sel(Switches_3), .Out(n2_to_1_selector_splitter_1_out));
  _8_bit_adder__splitter u_8_bit_adder_splitter_1 (
    .A_in(Switches), .B_in(n2_to_1_selector_splitter_1_out), .Out(out_6), .Carry_in(CI), .Carry_out(CO));
endmodule
